# Fritzing sketch MovingSkeleton (saved by Fritzing 0.9.3b)
breadboards: 1

parts:
  J1 = Basic Servo
  Composant1 = Arduino Uno (Rev3)
  R1 = Resistor [tolerance=±5% resistance=220 package=THT]
  LED2 = LED - 5mm [color="Red (633nm)" package="5 mm [THT]"]
  LED3 = LED - 5mm [color="Red (633nm)" package="5 mm [THT]"]

nets:
  GND: J1.gnd, Composant1.GND, R1.Pin_0, R1.Pin_1, LED2.cathode, LED3.cathode
  VCC: J1.vcc, Composant1.5V
  N1: J1.pulse, Composant1.D9_PWM
  N2: Composant1.D13/SCK, LED2.anode, LED3.anode
